# Fritzing sketch pool-keeper (saved by Fritzing 0.9.3b)
breadboards: 1

parts:
  Part1 = Adafruit Feather HUZZAH ESP8266 [part_number="Adafruit #2821"]  # not connected
  Part3 = Adafruit FeatherWing Proto [part_number="Adafruit #2884"]
  DHT1 = DHT22 Humidity and Temperature Sensor
  Part4 = Adafruit_BMP280

nets:
  GND: Part3.USB, Part3.A, Part3.GND, Part3.N$65, Part3.N$71, Part3.N$73, Part3.N$128, DHT1.GND, Part4.GND
  N1: Part3.I, Part3.RST
  N2: Part3.SCL, Part4.SCK/SCL
  N3: Part3.SDA, Part4.SDI/SDA
  VDD: Part3.3V, Part3.N$125, DHT1.VDD, Part4.VIN
  N4: Part3.H, Part3.N$122, Part3.N$126, DHT1.DATA
  N5: Part3.N$127, DHT1.NULL

custom parts:
  Adafruit Feather HUZZAH ESP8266: his is the Adafruit Feather HUZZAH ESP8266 - our take on an 'all-in-one' ESP8266 WiFi development board with built in USB and battery charging. Its an ESP8266 WiFi module with all the extras you need, ready to rock! We have other boards in the Feather family, check'em out here. At the Feather HUZZAH's heart is an ESP8266 WiFi microcontroller clocked at 80 MHz and at 3.3V logic. This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
  Adafruit FeatherWing Proto: This is the FeatherWing Proto - a prototyping add-on for all Feather boards. Using our Feather Stacking Headers or Feather Female Headers you can connect a FeatherWing on top or bottom of your Feather board and let the board take flight! This has a duplicate breakout for each pin on a Feather, as well as a bunch of plain grid proto holes. For GND and 3.3V, we give you a strip of connected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
  Adafruit_BMP280: Bosch has stepped up their game with their new BMP280 sensor, an environmental sensor with temperature, barometric pressure that is the next generation upgrade to the BMP085/BMP180/BMP183. This sensor is great for all sorts of weather sensing and can even be used in both I2C and SPI! This precision sensor from Bosch is the best low-cost, precision sensing solution for measuring barometric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
